// Logisim project FINAL.circ as structural Verilog: 5 circuits, main circuit main
module main (
);

  wire button_2_out, button_3_out, button_4_out, button_5_out, button_6_out, button_7_out, button_8_out,
       button_9_out, button_10_out, cdm_8_mark5_1_p1, cdm_8_mark5_1_p2, cdm_8_mark5_1_p4, cdm_8_mark5_1_p5,
       cdm_8_mark5_1_p6, cdm_8_mark5_1_p7, cdm_8_mark5_1_p8, Cl, code, data, decoder_1_out0, decoder_1_out1,
       gsdd_1_draw, gsdd_1_lose, gsdd_1_win, I_Osel, In_out_prime, IO_3_out, mem, nand_1_out, not_1_out,
       not_2_out, RAM, rst;
  wire [1:0] sdr_1_h0, sdr_1_h1, sdr_1_h2, sdr_1_v0, sdr_1_v1, sdr_1_v2;
  wire [2:2] tttc_1_hout, tttc_1_vout, tttc_2_vout, tttc_3_vout, tttc_4_hout, tttc_7_hout;
  wire [3:0] I_Oadr, tttc_1_l0, tttc_1_l1, tttc_1_l2, tttc_1_l3, tttc_2_l0, tttc_2_l1, tttc_2_l2, tttc_2_l3,
       tttc_3_l0, tttc_3_l1, tttc_3_l2, tttc_3_l3, tttc_4_l0, tttc_4_l1, tttc_4_l2, tttc_4_l3, tttc_5_l0,
       tttc_5_l1, tttc_5_l2, tttc_5_l3, tttc_6_l0, tttc_6_l1, tttc_6_l2, tttc_6_l3, tttc_7_l0, tttc_7_l1,
       tttc_7_l2, tttc_7_l3, tttc_8_l0, tttc_8_l1, tttc_8_l2, tttc_8_l3, tttc_9_l0, tttc_9_l1, tttc_9_l2,
       tttc_9_l3;
  wire [7:0] bpc_1_ready, cdm_8_mark5_1_p12, cdm_8_mark5_1_p13, I_Odat;
  wire [7:4] cdm_8_mark5_1_p11;

  and and_1 (I_Osel, not_1_out, Cl, data);
  // Probe on I_Odat
  LED led_1 (.in(gsdd_1_win));
  // Probe on cdm_8_mark5_1_p2
  // Probe on cdm_8_mark5_1_p5
  // Probe on cdm_8_mark5_1_p1
  // Probe on cdm_8_mark5_1_p4
  Clock clock_1 (.out(Cl));
  Button button_1 (.out(rst));
  LED led_2 (.in(gsdd_1_draw));
  LED led_3 (.in(gsdd_1_lose));
  GSDD gsdd_1 (
    .score(I_Odat[7:6]), .clock(decoder_1_out0), .win(gsdd_1_win), .lose(gsdd_1_lose), .draw(gsdd_1_draw),
    .reset(rst));
  // Probe on cdm_8_mark5_1_p7
  // Probe on cdm_8_mark5_1_p6
  // CdM_8_mark5 cdm_8_mark5_1: pin names not known; wires that end beside it: cdm_8_mark5_1_p1, cdm_8_mark5_1_p2, Cl, cdm_8_mark5_1_p4, cdm_8_mark5_1_p5, cdm_8_mark5_1_p6, cdm_8_mark5_1_p7, cdm_8_mark5_1_p8, mem, In_out_prime, {cdm_8_mark5_1_p11, I_Oadr}, cdm_8_mark5_1_p12, cdm_8_mark5_1_p13, {cdm_8_mark5_1_p11, I_Oadr}
  not not_1 (not_1_out, nand_1_out);
  nand nand_1 (nand_1_out, cdm_8_mark5_1_p11[4], cdm_8_mark5_1_p11[5], cdm_8_mark5_1_p11[6], cdm_8_mark5_1_p11[7]);
  and and_2 (RAM, nand_1_out, data);
  and IO_3 (IO_3_out, I_Osel, I_Oadr[0], I_Oadr[1], ~I_Oadr[2], ~I_Oadr[3]);  // AND_Gate
  SDR sdr_1 (
    .XY(I_Odat[5:2]), .symID(I_Odat[1:0]), .V0(sdr_1_v0), .V1(sdr_1_v1), .V2(sdr_1_v2),
    .clock(decoder_1_out0), .H2(sdr_1_h2), .H1(sdr_1_h1), .H0(sdr_1_h0));
  not not_2 (not_2_out, In_out_prime);
  assign cdm_8_mark5_1_p13 = In_out_prime ? I_Odat : 8'bz;  // Controlled_Buffer controlled_buffer_1
  Decoder #(.disabled(0)) decoder_1 (.out0(decoder_1_out0), .out1(decoder_1_out1), .sel(In_out_prime), .en(IO_3_out));
  // Probe on tttc_1_vout[2]
  Decoder #(.disabled(0)) decoder_2 (.out0(code), .out1(data), .sel(cdm_8_mark5_1_p8), .en(mem));
  assign I_Odat = not_2_out ? cdm_8_mark5_1_p12 : 8'bz;  // Controlled_Buffer controlled_buffer_2
  TTTC tttc_1 (
    .vout(tttc_1_vout[2]), .vin(sdr_1_h0), .hin(sdr_1_v0), .hout(tttc_1_hout[2]), .L0(tttc_1_l0),
    .L1(tttc_1_l1), .L2(tttc_1_l2), .L3(tttc_1_l3), .btn(button_2_out), .reset(rst));
  DotMatrix #(.inputtype("row"), .matrixcols(4), .matrixrows(4)) dotmatrix_1 (
    .row0(tttc_1_l0), .row1(tttc_1_l1), .row2(tttc_1_l2), .row3(tttc_1_l3));
  Button button_2 (.out(button_2_out));
  TTTC tttc_2 (
    .vout(tttc_2_vout[2]), .vin(sdr_1_h1), .hin(sdr_1_v0), .hout(tttc_1_hout[2]), .L0(tttc_2_l0),
    .L1(tttc_2_l1), .L2(tttc_2_l2), .L3(tttc_2_l3), .btn(button_3_out), .reset(rst));
  DotMatrix #(.inputtype("row"), .matrixcols(4), .matrixrows(4)) dotmatrix_2 (
    .row0(tttc_2_l0), .row1(tttc_2_l1), .row2(tttc_2_l2), .row3(tttc_2_l3));
  Button button_3 (.out(button_3_out));
  DotMatrix #(.inputtype("row"), .matrixcols(4), .matrixrows(4)) dotmatrix_3 (
    .row0(tttc_3_l0), .row1(tttc_3_l1), .row2(tttc_3_l2), .row3(tttc_3_l3));
  TTTC tttc_3 (
    .vout(tttc_3_vout[2]), .vin(sdr_1_h2), .hin(sdr_1_v0), .hout(tttc_1_hout[2]), .L0(tttc_3_l0),
    .L1(tttc_3_l1), .L2(tttc_3_l2), .L3(tttc_3_l3), .btn(button_4_out), .reset(rst));
  Button button_4 (.out(button_4_out));
  // Probe on tttc_2_vout[2]
  Pull_Resistor pull_resistor_1 (.node(I_Oadr[0]));
  Pull_Resistor pull_resistor_2 (.node(I_Oadr[1]));
  Pull_Resistor pull_resistor_3 (.node(I_Oadr[2]));
  Pull_Resistor pull_resistor_4 (.node(I_Oadr[3]));
  Pull_Resistor pull_resistor_5 (.node(cdm_8_mark5_1_p11[4]));
  Pull_Resistor pull_resistor_6 (.node(cdm_8_mark5_1_p11[5]));
  Pull_Resistor pull_resistor_7 (.node(cdm_8_mark5_1_p11[6]));
  Pull_Resistor pull_resistor_8 (.node(cdm_8_mark5_1_p11[7]));
  DotMatrix #(.inputtype("row"), .matrixcols(4), .matrixrows(4)) dotmatrix_4 (
    .row0(tttc_4_l0), .row1(tttc_4_l1), .row2(tttc_4_l2), .row3(tttc_4_l3));
  TTTC tttc_4 (
    .vout(tttc_1_vout[2]), .vin(sdr_1_h0), .hin(sdr_1_v1), .hout(tttc_4_hout[2]), .L0(tttc_4_l0),
    .L1(tttc_4_l1), .L2(tttc_4_l2), .L3(tttc_4_l3), .btn(button_5_out), .reset(rst));
  Button button_5 (.out(button_5_out));
  DotMatrix #(.inputtype("row"), .matrixcols(4), .matrixrows(4)) dotmatrix_5 (
    .row0(tttc_5_l0), .row1(tttc_5_l1), .row2(tttc_5_l2), .row3(tttc_5_l3));
  TTTC tttc_5 (
    .vout(tttc_2_vout[2]), .vin(sdr_1_h1), .hin(sdr_1_v1), .hout(tttc_4_hout[2]), .L0(tttc_5_l0),
    .L1(tttc_5_l1), .L2(tttc_5_l2), .L3(tttc_5_l3), .btn(button_6_out), .reset(rst));
  Button button_6 (.out(button_6_out));
  TTTC tttc_6 (
    .vout(tttc_3_vout[2]), .vin(sdr_1_h2), .hin(sdr_1_v1), .hout(tttc_4_hout[2]), .L0(tttc_6_l0),
    .L1(tttc_6_l1), .L2(tttc_6_l2), .L3(tttc_6_l3), .btn(button_7_out), .reset(rst));
  DotMatrix #(.inputtype("row"), .matrixcols(4), .matrixrows(4)) dotmatrix_6 (
    .row0(tttc_6_l0), .row1(tttc_6_l1), .row2(tttc_6_l2), .row3(tttc_6_l3));
  Button button_7 (.out(button_7_out));
  ROM rom_1 (.addr({cdm_8_mark5_1_p11, I_Oadr}), .data(I_Odat), .sel(code));
  RAM ram_1 (.addr({cdm_8_mark5_1_p11, I_Oadr}), .data(I_Odat), .sel(RAM), .clk(Cl), .ld(In_out_prime), .clr(rst));
  DotMatrix #(.inputtype("row"), .matrixcols(4), .matrixrows(4)) dotmatrix_7 (
    .row0(tttc_7_l0), .row1(tttc_7_l1), .row2(tttc_7_l2), .row3(tttc_7_l3));
  TTTC tttc_7 (
    .vout(tttc_1_vout[2]), .vin(sdr_1_h0), .hin(sdr_1_v2), .hout(tttc_7_hout[2]), .L0(tttc_7_l0),
    .L1(tttc_7_l1), .L2(tttc_7_l2), .L3(tttc_7_l3), .btn(button_8_out), .reset(rst));
  Button button_8 (.out(button_8_out));
  TTTC tttc_8 (
    .vout(tttc_2_vout[2]), .vin(sdr_1_h1), .hin(sdr_1_v2), .hout(tttc_7_hout[2]), .L0(tttc_8_l0),
    .L1(tttc_8_l1), .L2(tttc_8_l2), .L3(tttc_8_l3), .btn(button_9_out), .reset(rst));
  DotMatrix #(.inputtype("row"), .matrixcols(4), .matrixrows(4)) dotmatrix_8 (
    .row0(tttc_8_l0), .row1(tttc_8_l1), .row2(tttc_8_l2), .row3(tttc_8_l3));
  Button button_9 (.out(button_9_out));
  TTTC tttc_9 (
    .vout(tttc_3_vout[2]), .vin(sdr_1_h2), .hin(sdr_1_v2), .hout(tttc_7_hout[2]), .L0(tttc_9_l0),
    .L1(tttc_9_l1), .L2(tttc_9_l2), .L3(tttc_9_l3), .btn(button_10_out), .reset(rst));
  DotMatrix #(.inputtype("row"), .matrixcols(4), .matrixrows(4)) dotmatrix_9 (
    .row0(tttc_9_l0), .row1(tttc_9_l1), .row2(tttc_9_l2), .row3(tttc_9_l3));
  Button button_10 (.out(button_10_out));
  BPC bpc_1 (
    .V0(tttc_1_hout[2]), .V1(tttc_4_hout[2]), .V2(tttc_7_hout[2]), .ready(bpc_1_ready[7]),
    .XY(bpc_1_ready[3:0]), .H0(tttc_1_vout[2]), .H1(tttc_2_vout[2]), .H2(tttc_3_vout[2]),
    .enable(decoder_1_out1));
  assign I_Odat = decoder_1_out1 ? {bpc_1_ready[7], 3'b000, bpc_1_ready[3:0]} : 8'bz;  // Controlled_Buffer controlled_buffer_3

  // Other names for the same wires on the sheet: rd_wr_prime = In_out_prime

  // Notes on the sheet:
  //   RESET
  //   I win
  //   memory-mapped I/O
  //   H0
  //   H1
  //   H2
  //   V0
  //   V1
  //   instr memory
  //   contents of rom_1 (hex, n*v repeats v):
  //   12*0 1 2 4 5 6 8 9 a 0 4 8 1 5 9 2 6 a 0 5 a 2 5 8 ff cc f0 ee 3d d0 f3 b2 a e0 33 96 96 8e 8e a2 d3
  //   3 bc 8c ac b0 d6 56 d6 a5 d0 f3 b1 5 e1 45 ee 3f d6 47 d0 f3 b2 d0 80 84 12 d0 2 d3 0 1b ac d6 28 d3
  //   b fc 0 eb 7a fc 8f fd 8f b0 b5 71 e1 77 0 e0 77 fc b0 71 e1 77 89 5 e1 75 ee 87 ee 77 ee 91 8f ee 58
  //   d3 3 bc d1 9 74 e1 84 ee 9b d7 d6 3d d0 f3 d1 40 d2 0 ba 19 a1 d4 d0 f3 d1 80 d2 0 ba 19 a1 d4 d0 f3
  //   d1 c0 d2 0 ba 19 a1 d4 d3 b fc 0 eb d2 fc 8f fd 8f fe b0 b5 74 e1 cf 5 e0 cf 9 b5 5 e1 cf d1 1 a9 96
  //   96 16 d0 f3 a2 d3 3 bc 8c ac d6 56 d6 3d 8f ee a7 d0 b f1 b5 5 e0 dc 8c ee d4 f0 d2 1 a2 94 94 18 d1
  //   f3 a4 d3 3 bc 8c ac d6 56 d6 3d
  //   data memory
  //   V2
endmodule

// Tic Tac Toe
module TTTC (
  input  [1:0] vin,
  input  [1:0] hin,
  input  btn,
  input  reset,
  output vout,
  output [3:0] L0,
  output [3:0] L1,
  output [3:0] L2,
  output [3:0] L3,
  output hout
);

  wire and_1_out;
  wire [1:0] addr;

  and and_1 (and_1_out, hin[1], vin[1]);
  Register #(.width(2)) sym_reg (.D({vin[0], hin[0]}), .en(and_1_out), .Q(addr), .clk(and_1_out), .clr(reset));
  ROM #(.addrWidth(2), .dataWidth(16)) rom_1 (.addr(addr), .data({L3, L2, L1, L0}));  // open: sel
  Transistor #(.\type ("n"), .gate("br")) transistor_1 (.in(1'b1), .out(hout), .gate(btn));

  assign vout = hout;

  // Other names for the same wires on the sheet: hin_0 = hin[0]; hin_1 = hin[1]; vin_0 = vin[0]; vin_1 = vin[1]

  // Notes on the sheet:
  //   I/O Pins
  //   Internal
  //   addr = sym_reg
  //   Inputs: vin(2), hin(2), btn
  //   Outputs: vout, hout, L0(4), L1(4), L3(4)
  //   Latches: register(2) sym_reg
  //   ROMs: symbols(2->16)
  //   symID.split(0) = hin.split(0)
  //   symID.split(1) = vin.split(0)
  //   sym ID
  //   on rising_edge of (hin.split(1) ∧ vin.split(1))
  //   do: sym_reg := symID
  //   Signals: symID(2), addr(2), bitmap(16)
  //   ROM
  //   symbols [0] = 0000 for blank
  //   symbols [1] = f99f  for  nought
  //   symbols [2] = 9429 for cross
  //   symbols [3] = 0000 is not used
  //   contents of rom_1 (hex, n*v repeats v):
  //   0 f99f 9429
  //   bitmap
  //   bitmap = symbols[addr]
  //   L0 = bitmap.split(0:3)
  //   L1 = bitmap.split(4:7)
  //   L2 = bitmap.split(8:11)
  //   L3 = bitmap.split(12:15)
  //   hout = if btn then 1  else float 
  //   vout = if btn then 1  else float
endmodule

// LLL
module SDR (
  input  clock,
  input  [3:0] XY,
  input  [1:0] symID,
  output [1:0] V0,
  output [1:0] V1,
  output [1:0] V2,
  output [1:0] H2,
  output [1:0] H1,
  output [1:0] H0
);

  wire decoder_1_out0, decoder_1_out1, decoder_1_out2, decoder_2_out0, decoder_2_out1, decoder_2_out2;

  Pull_Resistor #(.pull(1)) pull_resistor_1 (.node(XY));
  Decoder #(.select(2)) decoder_1 (
    .out0(decoder_1_out0), .out1(decoder_1_out1), .out2(decoder_1_out2), .sel(XY[3:2]));  // open: out3, en
  assign H2 = decoder_1_out2 ? {clock, symID[1]} : 2'bz;  // Controlled_Buffer controlled_buffer_1
  assign H1 = decoder_1_out1 ? {clock, symID[1]} : 2'bz;  // Controlled_Buffer controlled_buffer_2
  assign H0 = decoder_1_out0 ? {clock, symID[1]} : 2'bz;  // Controlled_Buffer controlled_buffer_3
  Decoder #(.select(2)) decoder_2 (
    .out0(decoder_2_out0), .out1(decoder_2_out1), .out2(decoder_2_out2), .sel(XY[1:0]));  // open: out3, en
  assign V0 = decoder_2_out0 ? {clock, symID[0]} : 2'bz;  // Controlled_Buffer controlled_buffer_4
  assign V1 = decoder_2_out1 ? {clock, symID[0]} : 2'bz;  // Controlled_Buffer controlled_buffer_5
  assign V2 = decoder_2_out2 ? {clock, symID[0]} : 2'bz;  // Controlled_Buffer controlled_buffer_6

  // Notes on the sheet:
  //   I/O Pins
  //   Internal
  //   Inputs: symID(2), XY(4), clock
  //   Signals: xcoord(2), ycoord(2)
  //   Outputs: H0(2), H1(2), H2(2), V0(2), V1(2), V2(2)
  //   ycoord
  //   xcoord
  //   H0.split(0) = if xcoord is 0b00 then symID.split(1) else float
  //   H0.split(1) = if xcoord is 0b00 then clock else float
  //   H1.split(0) = if xcoord is 0b01 then symID.split(1) else float
  //   H1.split(1) = if xcoord is 0b01 then clock else float
  //   H2.split(0) = if xcoord is 0b10 then symID.split(1) else float
  //   H2.split(1) = if xcoord is 0b10 then clock else float
  //   V0.split(0) = if ycoord is 0b00 then symID.split(0) else float
  //   V0.split(1) = if ycoord is 0b00 then clock else float
  //   V1.split(0) = if ycoord is 0b01 then symID.split(0) else float
  //   V1.split(1) = if ycoord is 0b01 then clock else float
  //   V2.split(0) = if ycoord is 0b10 then symID.split(0) else float
  //   V2.split(1) = if ycoord is 0b10 then clock else float
endmodule

// BBB
module BPC (
  input  V0,
  input  V1,
  input  V2,
  input  H0,
  input  H1,
  input  H2,
  input  enable,
  output ready,
  output [3:0] XY
);

  wire not_1_out, not_2_out, or_1_out, or_2_out;
  wire [1:0] bitselector_1_out, bitselector_2_out;

  Pull_Resistor pull_resistor_1 (.node(V2));
  Pull_Resistor pull_resistor_2 (.node(V0));
  Pull_Resistor pull_resistor_3 (.node(V1));
  Pull_Resistor pull_resistor_4 (.node(H2));
  Pull_Resistor pull_resistor_5 (.node(H0));
  Pull_Resistor pull_resistor_6 (.node(H1));
  not not_1 (not_1_out, V0);
  not not_2 (not_2_out, H0);
  or or_1 (or_1_out, V0, V1, V2);
  BitSelector #(.width(4), .group(2)) bitselector_1 (.in({V2, V1, 2'b00}), .out(bitselector_1_out), .sel(not_1_out));
  BitSelector #(.width(4), .group(2)) bitselector_2 (.in({H2, H1, 2'b00}), .out(bitselector_2_out), .sel(not_2_out));
  or or_2 (or_2_out, H0, H1, H2);
  and and_1 (ready, or_1_out, or_2_out, enable);
  assign XY = enable ? {bitselector_2_out, bitselector_1_out} : 4'bz;  // Controlled_Buffer controlled_buffer_1
  Pull_Resistor pull_resistor_7 (.node(XY));

  // Notes on the sheet:
  //   I/O Pins
  //   Outputs: ready, XY(4)
  //   Inputs: H0, H1, H2, V0, V1, V2, enable
endmodule

module GSDD (
  input  [1:0] score,
  input  clock,
  input  reset,
  output win,
  output lose,
  output draw
);

  wire [1:0] state_q;

  Register #(.width(2)) state (.D(score), .en(clock), .Q(state_q), .clk(clock), .clr(reset));
  and and_1 (win, ~state_q[0], state_q[1]);  // AND_Gate
  and and_2 (lose, state_q[0], ~state_q[1]);  // AND_Gate
  and and_3 (draw, state_q[0], state_q[1]);

  // Notes on the sheet:
  //   I/O Pins
  //   Internal
  //   Inputs: score(2), clock
  //   Outputs: win, lose, draw
  //   lose = if state is 0b10 then 1 else 0
  //   win = if state is 0b01 then 1 else 0
  //   draw = if state is 0b11 then 1 else 0
  //   Latches: register(2) state
endmodule
