// Logisim project project2.circ as structural Verilog: 5 circuits, main circuit main
module main (
  input  [2:0] in_1,
  input  [2:0] in_2,
  output [7:0] out_3,
  output [7:0] out_4,
  output [7:0] out_5,
  output [7:0] out_6,
  output [7:0] out_7,
  output [7:0] out_8
);

  wire button_2_out, button_3_out, button_4_out, button_5_out, button_6_out, button_7_out, button_8_out,
       button_9_out, button_10_out, button_11_out, cdm_8_mark5_1_p7, Cl, code, data, decoder_1_out0,
       decoder_1_out1, gsdd_1_draw, gsdd_1_lose, gsdd_1_win, I_Osel, In_out_prime, IO_3_out, mem, nand_1_out,
       not_1_out, not_2_out, RAM, rst;
  wire [1:0] sdr_1_h0, sdr_1_h1, sdr_1_h2, sdr_1_v0, sdr_1_v2;
  wire [2:2] tttc_1_hout, tttc_1_vout, tttc_2_vout, tttc_3_vout, tttc_4_hout;
  wire [3:0] I_Oadr, tttc_1_l0, tttc_1_l1, tttc_1_l2, tttc_1_l3, tttc_2_l0, tttc_2_l1, tttc_2_l2, tttc_2_l3,
       tttc_3_l0, tttc_3_l1, tttc_3_l2, tttc_3_l3, tttc_4_l0, tttc_4_l1, tttc_4_l2, tttc_4_l3, tttc_5_l0,
       tttc_5_l1, tttc_5_l2, tttc_5_l3, tttc_6_l0, tttc_6_l1, tttc_6_l2, tttc_6_l3, tttc_7_l0, tttc_7_l1,
       tttc_7_l2, tttc_7_l3, tttc_8_l0, tttc_8_l1, tttc_8_l2, tttc_8_l3, tttc_9_l0, tttc_9_l1, tttc_9_l2,
       tttc_9_l3, tttc_10_l0, tttc_10_l1, tttc_10_l2, tttc_10_l3;
  wire [7:0] bpc_1_ready, cdm_8_mark5_1_p11, cdm_8_mark5_1_p12, I_Odat;
  wire [7:4] cdm_8_mark5_1_p10;

  and and_1 (I_Osel, not_1_out, Cl, data);
  // Probe on I_Odat
  Button button_1 (.out(Cl));
  Clock clock_1 (.out(Cl));
  LED led_1 (.in(gsdd_1_win));
  LED led_2 (.in(gsdd_1_lose));
  // CdM_8_mark5 cdm_8_mark5_1: pin names not known; wires that end beside it: out_8, out_7, out_6, out_5, out_4, out_3, cdm_8_mark5_1_p7, mem, In_out_prime, {cdm_8_mark5_1_p10, I_Oadr}, cdm_8_mark5_1_p11, cdm_8_mark5_1_p12, {cdm_8_mark5_1_p10, I_Oadr}
  not not_1 (not_1_out, nand_1_out);
  nand nand_1 (nand_1_out, cdm_8_mark5_1_p10[4], cdm_8_mark5_1_p10[5], cdm_8_mark5_1_p10[6], cdm_8_mark5_1_p10[7]);
  and and_2 (RAM, nand_1_out, data);
  and IO_3 (IO_3_out, I_Osel, I_Oadr[0], I_Oadr[1], ~I_Oadr[2], ~I_Oadr[3]);  // AND_Gate
  LED led_3 (.in(gsdd_1_draw));
  GSDD gsdd_1 (
    .score(I_Odat[7:6]), .clock(decoder_1_out0), .win(gsdd_1_win), .lose(gsdd_1_lose), .draw(gsdd_1_draw),
    .reset(rst));
  SDR sdr_1 (
    .XY(I_Odat[5:2]), .symID(I_Odat[1:0]), .clock(decoder_1_out0), .V0(sdr_1_v0), .V1(sdr_1_v0),
    .V2(sdr_1_v2), .H0(sdr_1_h0), .H1(sdr_1_h1), .H2(sdr_1_h2));
  not not_2 (not_2_out, In_out_prime);
  assign cdm_8_mark5_1_p12 = In_out_prime ? I_Odat : 8'bz;  // Controlled_Buffer controlled_buffer_1
  Decoder #(.disabled(0)) decoder_1 (.out0(decoder_1_out0), .out1(decoder_1_out1), .sel(In_out_prime), .en(IO_3_out));
  Decoder decoder_2 (.out0(code), .out1(data), .sel(cdm_8_mark5_1_p7), .en(mem));
  assign I_Odat = not_2_out ? cdm_8_mark5_1_p11 : 8'bz;  // Controlled_Buffer controlled_buffer_2
  TTTC tttc_1 (
    .vout(tttc_1_vout[2]), .vin(sdr_1_h0), .hin(sdr_1_v2), .hout(tttc_1_hout[2]), .L0(tttc_1_l0),
    .L1(tttc_1_l1), .L2(tttc_1_l2), .L3(tttc_1_l3), .in_3(button_2_out));
  DotMatrix #(.inputtype("row"), .matrixcols(4), .matrixrows(4)) dotmatrix_1 (
    .row0(tttc_1_l0), .row1(tttc_1_l1), .row2(tttc_1_l2), .row3(tttc_1_l3));
  Button button_2 (.out(button_2_out));
  DotMatrix #(.inputtype("row"), .matrixcols(4), .matrixrows(4)) dotmatrix_2 (
    .row0(tttc_2_l0), .row1(tttc_2_l1), .row2(tttc_2_l2), .row3(tttc_2_l3));
  TTTC tttc_2 (
    .vout(tttc_2_vout[2]), .vin(sdr_1_h1), .hin(sdr_1_v2), .hout(tttc_1_hout[2]), .L0(tttc_2_l0),
    .L1(tttc_2_l1), .L2(tttc_2_l2), .L3(tttc_2_l3), .in_3(button_3_out));
  Button button_3 (.out(button_3_out));
  TTTC tttc_3 (
    .vout(tttc_3_vout[2]), .vin(sdr_1_h2), .hin(sdr_1_v2), .hout(tttc_1_hout[2]), .L0(tttc_3_l0),
    .L1(tttc_3_l1), .L2(tttc_3_l2), .L3(tttc_3_l3), .in_3(button_4_out));
  DotMatrix #(.inputtype("row"), .matrixcols(4), .matrixrows(4)) dotmatrix_3 (
    .row0(tttc_3_l0), .row1(tttc_3_l1), .row2(tttc_3_l2), .row3(tttc_3_l3));
  Button button_4 (.out(button_4_out));
  Pull_Resistor pull_resistor_1 (.node(I_Oadr[0]));
  Pull_Resistor pull_resistor_2 (.node(I_Oadr[1]));
  Pull_Resistor pull_resistor_3 (.node(I_Oadr[2]));
  Pull_Resistor pull_resistor_4 (.node(I_Oadr[3]));
  Pull_Resistor pull_resistor_5 (.node(cdm_8_mark5_1_p10[4]));
  Pull_Resistor pull_resistor_6 (.node(cdm_8_mark5_1_p10[5]));
  Pull_Resistor pull_resistor_7 (.node(cdm_8_mark5_1_p10[6]));
  Pull_Resistor pull_resistor_8 (.node(cdm_8_mark5_1_p10[7]));
  TTTC tttc_4 (
    .vout(tttc_1_vout[2]), .vin(sdr_1_h0), .hin(sdr_1_v0), .hout(tttc_4_hout[2]), .L0(tttc_4_l0),
    .L1(tttc_4_l1), .L2(tttc_4_l2), .L3(tttc_4_l3), .in_3(button_5_out));
  DotMatrix #(.inputtype("row"), .matrixcols(4), .matrixrows(4)) dotmatrix_4 (
    .row0(tttc_4_l0), .row1(tttc_4_l1), .row2(tttc_4_l2), .row3(tttc_4_l3));
  Button button_5 (.out(button_5_out));
  TTTC tttc_5 (
    .vout(tttc_2_vout[2]), .vin(sdr_1_h1), .hin(sdr_1_v0), .hout(tttc_4_hout[2]), .L0(tttc_5_l0),
    .L1(tttc_5_l1), .L2(tttc_5_l2), .L3(tttc_5_l3), .in_3(button_6_out));
  DotMatrix #(.inputtype("row"), .matrixcols(4), .matrixrows(4)) dotmatrix_5 (
    .row0(tttc_5_l0), .row1(tttc_5_l1), .row2(tttc_5_l2), .row3(tttc_5_l3));
  Button button_6 (.out(button_6_out));
  DotMatrix #(.inputtype("row"), .matrixcols(4), .matrixrows(4)) dotmatrix_6 (
    .row0(tttc_6_l0), .row1(tttc_6_l1), .row2(tttc_6_l2), .row3(tttc_6_l3));
  TTTC tttc_6 (
    .vout(tttc_3_vout[2]), .vin(sdr_1_h2), .hin(sdr_1_v0), .hout(tttc_4_hout[2]), .L0(tttc_6_l0),
    .L1(tttc_6_l1), .L2(tttc_6_l2), .L3(tttc_6_l3), .in_3(button_7_out));
  Button button_7 (.out(button_7_out));
  ROM rom_1 (.addr({cdm_8_mark5_1_p10, I_Oadr}), .data(I_Odat), .sel(code));
  RAM ram_1 (.addr({cdm_8_mark5_1_p10, I_Oadr}), .data(I_Odat), .sel(RAM), .clk(Cl), .ld(In_out_prime));  // open: clr
  // Probe on tttc_4_hout[2]
  DotMatrix #(.inputtype("row"), .matrixcols(4), .matrixrows(4)) dotmatrix_7 (
    .row0(tttc_7_l0), .row1(tttc_7_l1), .row2(tttc_7_l2), .row3(tttc_7_l3));
  TTTC tttc_7 (
    .vout(tttc_1_vout[2]), .vin(sdr_1_h0), .hin(sdr_1_v0), .hout(tttc_4_hout[2]), .L0(tttc_7_l0),
    .L1(tttc_7_l1), .L2(tttc_7_l2), .L3(tttc_7_l3), .in_3(button_8_out));
  Button button_8 (.out(button_8_out));
  DotMatrix #(.inputtype("row"), .matrixcols(4), .matrixrows(4)) dotmatrix_8 (
    .row0(tttc_8_l0), .row1(tttc_8_l1), .row2(tttc_8_l2), .row3(tttc_8_l3));
  TTTC tttc_8 (
    .vout(tttc_2_vout[2]), .vin(sdr_1_h1), .hin(sdr_1_v0), .hout(tttc_4_hout[2]), .L0(tttc_8_l0),
    .L1(tttc_8_l1), .L2(tttc_8_l2), .L3(tttc_8_l3), .in_3(button_9_out));
  Button button_9 (.out(button_9_out));
  TTTC tttc_9 (
    .vout(tttc_3_vout[2]), .vin(sdr_1_h2), .hin(sdr_1_v0), .hout(tttc_4_hout[2]), .L0(tttc_9_l0),
    .L1(tttc_9_l1), .L2(tttc_9_l2), .L3(tttc_9_l3), .in_3(button_10_out));
  DotMatrix #(.inputtype("row"), .matrixcols(4), .matrixrows(4)) dotmatrix_9 (
    .row0(tttc_9_l0), .row1(tttc_9_l1), .row2(tttc_9_l2), .row3(tttc_9_l3));
  Button button_10 (.out(button_10_out));
  assign I_Odat = decoder_1_out1 ? {bpc_1_ready[7], 3'b000, bpc_1_ready[3:0]} : 8'bz;  // Controlled_Buffer controlled_buffer_3
  BPC bpc_1 (
    .V0(tttc_1_hout[2]), .V1(tttc_4_hout[2]), .V2(tttc_4_hout[2]), .ready(bpc_1_ready[7]),
    .XY(bpc_1_ready[3:0]), .H0(tttc_1_vout[2]), .H1(tttc_2_vout[2]), .H2(tttc_3_vout[2]),
    .enable(decoder_1_out1));
  TTTC tttc_10 (
    .vout(in_1[2]), .vin(in_1[1:0]), .hin(in_2[1:0]), .hout(in_2[2]), .L0(tttc_10_l0), .L1(tttc_10_l1),
    .L2(tttc_10_l2), .L3(tttc_10_l3), .in_3(button_11_out));
  DotMatrix #(.inputtype("row"), .matrixcols(4), .matrixrows(4)) dotmatrix_10 (
    .row0(tttc_10_l0), .row1(tttc_10_l1), .row2(tttc_10_l2), .row3(tttc_10_l3));
  Button button_11 (.out(button_11_out));

  // Other names for the same wires on the sheet: rd_wr_prime = In_out_prime

  // Notes on the sheet:
  //   reset
  //   I win
  //   memory-mapped I/O
  //   H0
  //   H1
  //   H2
  //   V0
  //   V1
  //   instr memory
  //   data memory
  //   V2
endmodule

// Tic Tac Toe
module TTTC (
  input  [1:0] vin,
  input  [1:0] hin,
  input  in_3,
  output vout,
  output [3:0] L0,
  output [3:0] L1,
  output [3:0] L2,
  output [3:0] L3,
  output hout
);

  wire and_1_out;
  wire [1:0] addr;

  and and_1 (and_1_out, hin[1], vin[1]);
  Register #(.width(2)) sym_reg (.D({vin[1], hin[0]}), .en(and_1_out), .Q(addr), .clk(and_1_out));  // open: clr
  ROM #(.addrWidth(2), .dataWidth(16)) rom_1 (.addr(addr), .data({L3, L2, L1, L0}));  // open: sel
  Transistor #(.\type ("n"), .gate("br")) transistor_1 (.in(1'b0), .out(hout), .gate(in_3));

  assign vout = hout;

  // Other names for the same wires on the sheet: hin_0 = hin[0]; hin_1 = hin[1]; vin_0 = vin[0]; vin_1 = vin[1]

  // Notes on the sheet:
  //   I/O Pins
  //   Internal
  //   addr = sym_reg
  //   Inputs: vin(2), hin(2), btn
  //   Outputs: vout, hout, L0(4), L1(4), L3(4)
  //   Latches: register(2) sym_reg
  //   ROMs: symbols(2->16)
  //   symID.split(0) = hin.split(0)
  //   symID.split(1) = vin.split(0)
  //   sym ID
  //   on rising_edge of (hin.split(1) ∧ vin.split(1))
  //   do: sym_reg := symID
  //   Signals: symID(2), addr(2), bitmap(16)
  //   ROM
  //   symbols [0] = 0000 for blank
  //   symbols [1] = 9429 for nought
  //   symbols [2] = f99f  for  cross
  //   symbols [3] = 0000 is not used
  //   contents of rom_1 (hex, n*v repeats v):
  //   0 f99f 9429
  //   bitmap
  //   bitmap = symbols[addr]
  //   L0 = bitmap.split(0:3)
  //   L1 = bitmap.split(4:7)
  //   L2 = bitmap.split(8:11)
  //   L3 = bitmap.split(12:15)
  //   hout = if btn then 0 else float 
  //   vout = if btn then 0 else float
endmodule

// LLL
module SDR (
  input  clock,
  input  [3:0] XY,
  input  [1:0] symID,
  output [1:0] H0,
  output [1:0] H1,
  output [1:0] H2,
  output [1:0] V0,
  output [1:0] V1,
  output [1:0] V2
);

  wire decoder_1_out0, decoder_1_out1, decoder_1_out2, decoder_2_out0, decoder_2_out1, decoder_2_out2;

  Pull_Resistor #(.pull(1)) pull_resistor_1 (.node(XY));
  Decoder #(.select(2)) decoder_1 (
    .out0(decoder_1_out0), .out1(decoder_1_out1), .out2(decoder_1_out2), .sel(XY[3:2]));  // open: out3, en
  assign V0 = decoder_1_out2 ? {clock, symID[1]} : 2'bz;  // Controlled_Buffer controlled_buffer_1
  assign V1 = decoder_1_out1 ? {clock, symID[1]} : 2'bz;  // Controlled_Buffer controlled_buffer_2
  assign V2 = decoder_1_out0 ? {clock, symID[1]} : 2'bz;  // Controlled_Buffer controlled_buffer_3
  Decoder #(.select(2)) decoder_2 (
    .out0(decoder_2_out0), .out1(decoder_2_out1), .out2(decoder_2_out2), .sel(XY[1:0]));  // open: out3, en
  assign H0 = decoder_2_out0 ? {clock, symID[0]} : 2'bz;  // Controlled_Buffer controlled_buffer_4
  assign H1 = decoder_2_out1 ? {clock, symID[0]} : 2'bz;  // Controlled_Buffer controlled_buffer_5
  assign H2 = decoder_2_out2 ? {clock, symID[0]} : 2'bz;  // Controlled_Buffer controlled_buffer_6

  // Notes on the sheet:
  //   I/O Pins
  //   Internal
  //   Inputs: symID(2), XY(4), clock
  //   Signals: xcoord(2), ycoord(2)
  //   Outputs: H0(2), H1(2), H2(2), V0(2), V1(2), V2(2)
  //   xcoord
  //   ycoord
endmodule

// BBB
module BPC (
  input  V0,
  input  V1,
  input  V2,
  input  H0,
  input  H1,
  input  H2,
  input  enable,
  output ready,
  output [3:0] XY
);

  wire not_1_out, not_2_out, or_1_out, or_2_out;
  wire [1:0] bitselector_1_out, bitselector_2_out;

  Pull_Resistor pull_resistor_1 (.node(V2));
  Pull_Resistor pull_resistor_2 (.node(V1));
  Pull_Resistor pull_resistor_3 (.node(V0));
  Pull_Resistor pull_resistor_4 (.node(H1));
  Pull_Resistor pull_resistor_5 (.node(H2));
  Pull_Resistor pull_resistor_6 (.node(H0));
  not not_1 (not_1_out, V0);
  not not_2 (not_2_out, H0);
  BitSelector #(.width(4), .group(2)) bitselector_1 (.in({V2, V1, 2'b00}), .out(bitselector_1_out), .sel(not_1_out));
  BitSelector #(.width(4), .group(2)) bitselector_2 (.in({H2, H1, 2'b00}), .out(bitselector_2_out), .sel(not_2_out));
  or or_1 (or_1_out, H0, H1, H2);
  or or_2 (or_2_out, V0, V1, V2);
  and and_1 (ready, or_2_out, or_1_out, enable);
  assign XY = enable ? {bitselector_2_out, bitselector_1_out} : 4'bz;  // Controlled_Buffer controlled_buffer_1
  Pull_Resistor pull_resistor_7 (.node(XY));

  // Notes on the sheet:
  //   I/O Pins
  //   Internal
  //   Outputs: ready, XY(4)
  //   Inputs: H0, H1, H2, V0, V1, V2, reset
  //   Latches: register(4) XY_reg, RS ready_flag
  //   Signals: xcoord(2), ycoord(2), XY(4), coord(4), b_press, btn, rst
endmodule

module GSDD (
  input  [1:0] score,
  input  clock,
  input  reset,
  output win,
  output lose,
  output draw
);

  wire [1:0] state_q;

  Register #(.width(2)) state (.D(score), .en(clock), .Q(state_q), .clk(clock), .clr(reset));
  and and_1 (win, ~state_q[0], state_q[1]);  // AND_Gate
  and and_2 (lose, state_q[0], ~state_q[1]);  // AND_Gate
  and and_3 (draw, state_q[0], state_q[1]);

  // Notes on the sheet:
  //   I/O Pins
  //   Internal
  //   Inputs: score(2), clock
  //   Outputs: win, lose, draw
  //   lose = if state is 0b00 then 1 else 0
  //   win = if state is 0b01 then 1 else 0
  //   lose = if state is 0b00 then 1 else 0
  //   Latches: register(2) state
endmodule
